# Fritzing sketch ups (saved by Fritzing 0.9.2b)
circuit board: 9.05929cm x 8.57955cm
breadboards: 1

parts:
  Part1 = Arduino Nano (Rev3.0)
  Part2 = Power Cell LiPo Charger/Booster
  U2 = LIPO-2000mAh [package=lipo-2000]
  U1 = Switching step-up voltage regulator [package=sot23-5]
  R1 = Resistor [tolerance=±5% resistance=10k package=THT]
  X1 = USB Connectors [package=usb-a-s]
  Q1 = Basic FET P-Channel [package="D2Pak [SMD]"]
  C1 = Electrolytic Capacitor [capacitance=1000µF package="300 mil [THT, electrolytic]"]
  J1 = Power Jack [package=power_jack_pth_lock]
  U4 = ACS712 [package=so08]
  R2 = Resistor [tolerance=±5% resistance=10k package="1206 [SMD]"]
  R3 = Resistor [tolerance=±5% resistance=8.2k package="1206 [SMD]"]
  R4 = Resistor [tolerance=±5% resistance=8.2k package="1206 [SMD]"]
  Mains-On = LED - 5mm [color="Red (633nm)" package="5 mm [THT]"]
  R5 = Resistor [tolerance=±5% resistance=10k package="1206 [SMD]"]
  R6 = Resistor [tolerance=±5% resistance=8.2k package="1206 [SMD]"]
  R7 = Resistor [tolerance=±5% resistance=8.2k package="1206 [SMD]"]
  Charging = LED - 5mm [color="Red (633nm)" package="5 mm [THT]"]
  U5 = RELAY [package=relay-t9a-2]
  D1 = Schottky Diode [part_number=1N5817 package="Melf DO-213 AB [SMD]"]

nets:
  GND: Part1.GND, Part2.GND, U2.-, U1.GND, R1.Pin_0, J1.GND, J1.GNDBREAK, U4.IP-, U4.GND, R4.Pin_0, Mains-On.cathode, R7.Pin_0, Charging.cathode, U5.COIL1
  N1: Part1.D2, R1.Pin_1, U5.COIL2, D1.cathode
  N2: Part1.D3, Q1.Gate
  N3: Part1.D7, Charging.anode
  N4: Part1.D8, Mains-On.anode
  N5: Part1.5V, Q1.drain, U5.MAIN
  N6: Part1.A2, R5.Pin_0, R6.Pin_1
  N7: Part1.A1, R2.Pin_0, R3.Pin_1
  N8: Part1.A0, U4.VOUT
  3V3: Part1.AREF, Part1.3V3, U4.VCC
  N9: Part2.VCC, U1.LX
  N10: Part2.5VIN, J1.PWR, U5.NO, D1.anode
  N11: Part2.VBATT, U2.+, R2.Pin_1
  N12: U1.OUT, U5.NC
  N13: X1.GND, C1.-, U4.IP+
  N14: X1.VBUS, Q1.source, C1.+, R5.Pin_1
  N15: R3.Pin_0, R4.Pin_1
  N16: R6.Pin_0, R7.Pin_1
